# Fritzing sketch poc-setup (saved by Fritzing 0.9.3b)
breadboards: 1

parts:
  U1 = NodeMCU V1.0
  DS1 = DS18B20 1-Wire Temperature Sensor [part_number=DS18B20]
  R1 = Resistor [tolerance=±5% resistance=4.7k package=THT]
  DS2 = DS18B20 1-Wire Temperature Sensor [part_number=DS18B20]

nets:
  N1: U1.D1, DS1.DQ, R1.Pin_1, DS2.DQ
  VDD: U1.3V3, DS1.VDD, R1.Pin_0, DS2.VDD
  GND: U1.GND, DS1.GND, DS2.GND

custom parts:
  NodeMCU V1.0: ESP8266 based NodeMCU
